// Logisim project mine.circ as structural Verilog: 10 circuits, main circuit register
module main (
  input  [7:0] data_test,
  input  OE,
  input  Res,
  input  in_4,
  input  [3:0] in_5,
  input  in_6,
  input  in_7,
  input  in_8,
  input  in_9,
  input  in_10,
  input  [2:0] in_11,
  input  in_12,
  input  in_13,
  input  in_14,
  output [3:0] out_15,
  output [3:0] out_16,
  output [7:0] out_17,
  output [7:0] out_18,
  output [7:0] out_19,
  output [7:0] out_20,
  output [7:0] out_21,
  output [7:0] out_22,
  output out_23,
  output [7:0] out_24,
  output [2:0] out_25
);

  wire clock_1_out, control_unit_1_1_c0, control_unit_1_1_c1, control_unit_1_1_c2, control_unit_1_1_c3,
       control_unit_1_1_c4, control_unit_1_1_c5, control_unit_1_1_c6, control_unit_1_1_c7,
       control_unit_1_1_c8, control_unit_1_1_c9, control_unit_1_1_c10, control_unit_1_1_c11,
       control_unit_2_1_c12, control_unit_2_1_c13, control_unit_2_1_c14, control_unit_2_1_c15;
  wire [3:0] bitselector_2_out, controlled_buffer_1_out, mar_1_out;
  wire [7:0] bit_extender_1_out, bit_extender_2_out, n8bit_alu_1_out_8, register_3_out;
  wire [15:0] decimal_decoder_4_output;
  wire [30:16] decimal_decoder_4_output_2;
  wire [31:0] decimal_decoder_1_output, decimal_decoder_2_output, decimal_decoder_3_output,
       decimal_decoder_5_output;

  Clock clock_1 (.out(clock_1_out));
  assign controlled_buffer_1_out = control_unit_1_1_c0 ? out_15 : 4'bz;  // Controlled_Buffer controlled_buffer_1
  Counter #(.width(4), .max('h3)) counter_1 (
    .D(controlled_buffer_1_out), .count(control_unit_1_1_c1), .Q(out_15), .clk(clock_1_out), .clr(Res));  // open: load, carry
  register register_1 (
    .In(n8bit_alu_1_out_8), .WE(control_unit_2_1_c12), .CLK(clock_1_out), .Res(in_8), .StoredD(out_19));  // open: OE, Out
  register register_2 (
    .In(n8bit_alu_1_out_8), .WE(control_unit_2_1_c13), .CLK(clock_1_out), .Res(in_14), .StoredD(out_24));  // open: OE, Out
  assign bit_extender_1_out = {{4{1'b0}}, out_15};  // Bit_Extender bit_extender_1
  decimal_decoder decimal_decoder_1 (.Input(out_19), .Output(decimal_decoder_1_output));
  _8bit_alu u_8bit_alu_1 (
    .in_4(out_19), .in_5(out_24), .in_2(in_9), .in_1(in_10), .in_3(in_11), .out_7(out_20),
    .out_8(n8bit_alu_1_out_8), .in_6(control_unit_1_1_c11), .out_9(out_23));
  decimal_decoder decimal_decoder_2 (.Input(bit_extender_1_out), .Output(decimal_decoder_2_output));
  register register_3 (
    .In(n8bit_alu_1_out_8), .WE(control_unit_1_1_c7), .CLK(clock_1_out), .OE(control_unit_1_1_c8),
    .Out(register_3_out), .StoredD(out_17));  // open: Res
  decimal_decoder decimal_decoder_3 (.Input(out_24), .Output(decimal_decoder_3_output));
  _7_Segment_Display u_7_segment_display_1 (
    .g(decimal_decoder_2_output[3]), .f(decimal_decoder_2_output[2]), .a(decimal_decoder_2_output[1]),
    .b(decimal_decoder_2_output[0]), .e(decimal_decoder_2_output[19]), .d(decimal_decoder_2_output[18]),
    .c(decimal_decoder_2_output[17]), .dp(decimal_decoder_2_output[16]));
  _7_Segment_Display u_7_segment_display_2 (
    .g(decimal_decoder_1_output[15]), .f(decimal_decoder_1_output[14]), .a(decimal_decoder_1_output[13]),
    .b(decimal_decoder_1_output[12]), .e(decimal_decoder_1_output[31]), .d(decimal_decoder_1_output[30]),
    .c(decimal_decoder_1_output[29]), .dp(decimal_decoder_1_output[28]));
  _7_Segment_Display u_7_segment_display_3 (
    .g(decimal_decoder_1_output[11]), .f(decimal_decoder_1_output[10]), .a(decimal_decoder_1_output[9]),
    .b(decimal_decoder_1_output[8]), .e(decimal_decoder_1_output[27]), .d(decimal_decoder_1_output[26]),
    .c(decimal_decoder_1_output[25]), .dp(decimal_decoder_1_output[24]));
  _7_Segment_Display u_7_segment_display_4 (
    .g(decimal_decoder_1_output[3]), .f(decimal_decoder_1_output[2]), .a(decimal_decoder_1_output[1]),
    .b(decimal_decoder_1_output[0]), .e(decimal_decoder_1_output[19]), .d(decimal_decoder_1_output[18]),
    .c(decimal_decoder_1_output[17]), .dp(decimal_decoder_1_output[16]));
  _7_Segment_Display u_7_segment_display_5 (
    .g(decimal_decoder_1_output[7]), .f(decimal_decoder_1_output[6]), .a(decimal_decoder_1_output[5]),
    .b(decimal_decoder_1_output[4]), .e(decimal_decoder_1_output[23]), .d(decimal_decoder_1_output[22]),
    .c(decimal_decoder_1_output[21]), .dp(decimal_decoder_1_output[20]));
  _7_Segment_Display u_7_segment_display_6 (
    .g(decimal_decoder_3_output[11]), .f(decimal_decoder_3_output[10]), .a(decimal_decoder_3_output[8]),
    .b(decimal_decoder_3_output[8]), .e(decimal_decoder_3_output[27]), .d(decimal_decoder_3_output[26]),
    .c(decimal_decoder_3_output[25]), .dp(decimal_decoder_3_output[24]));
  _7_Segment_Display u_7_segment_display_7 (
    .g(decimal_decoder_3_output[15]), .f(decimal_decoder_3_output[14]), .a(decimal_decoder_3_output[13]),
    .b(decimal_decoder_3_output[12]), .e(decimal_decoder_3_output[31]), .d(decimal_decoder_3_output[30]),
    .c(decimal_decoder_3_output[29]), .dp(decimal_decoder_3_output[28]));
  _7_Segment_Display u_7_segment_display_8 (
    .g(decimal_decoder_3_output[7]), .f(decimal_decoder_3_output[6]), .a(decimal_decoder_3_output[5]),
    .b(decimal_decoder_3_output[4]), .e(decimal_decoder_3_output[23]), .d(decimal_decoder_3_output[22]),
    .c(decimal_decoder_3_output[21]), .dp(decimal_decoder_3_output[20]));
  _7_Segment_Display u_7_segment_display_9 (
    .g(decimal_decoder_3_output[3]), .f(decimal_decoder_3_output[2]), .a(decimal_decoder_3_output[1]),
    .b(decimal_decoder_3_output[0]), .e(decimal_decoder_3_output[19]), .d(decimal_decoder_3_output[18]),
    .c(decimal_decoder_3_output[17]), .dp(decimal_decoder_3_output[16]));
  BitSelector #(.group(4)) bitselector_1 (.in(register_3_out), .out(controlled_buffer_1_out), .sel(1'b0));
  LED led_1 (.in(n8bit_alu_1_out_8[7]));
  LED led_2 (.in(n8bit_alu_1_out_8[6]));
  LED led_3 (.in(n8bit_alu_1_out_8[5]));
  assign n8bit_alu_1_out_8 = in_4 ? data_test : 8'bz;  // Controlled_Buffer controlled_buffer_2
  LED led_4 (.in(n8bit_alu_1_out_8[4]));
  LED led_5 (.in(n8bit_alu_1_out_8[2]));
  LED led_6 (.in(n8bit_alu_1_out_8[3]));
  LED led_7 (.in(n8bit_alu_1_out_8[0]));
  LED led_8 (.in(n8bit_alu_1_out_8[1]));
  assign n8bit_alu_1_out_8 = control_unit_1_1_c5 ? out_18 : 8'bz;  // Controlled_Buffer controlled_buffer_3
  mar mar_1 (
    .In(controlled_buffer_1_out), .WE(control_unit_1_1_c9), .CLK(clock_1_out), .Res(in_6),
    .OE(control_unit_1_1_c10), .Out(mar_1_out), .Stored_D(out_16));
  register register_4 (
    .In(n8bit_alu_1_out_8), .WE(control_unit_1_1_c4), .CLK(clock_1_out), .OE(control_unit_1_1_c6),
    .Out(n8bit_alu_1_out_8), .StoredD(out_18));  // open: Res
  register register_5 (
    .In(n8bit_alu_1_out_8), .WE(control_unit_2_1_c15), .CLK(clock_1_out), .Res(in_12),
    .OE(control_unit_2_1_c14), .Out(n8bit_alu_1_out_8), .StoredD(out_21));
  decimal_decoder decimal_decoder_4 (
    .Input(out_21),
    .Output({decimal_decoder_4_output[15], decimal_decoder_4_output_2, decimal_decoder_4_output}));
  assign out_22 = in_13 ? ~out_21 : 8'bz;  // Controlled_Inverter controlled_inverter_1
  _7_Segment_Display u_7_segment_display_10 (
    .g(decimal_decoder_4_output[15]), .f(decimal_decoder_4_output[14]), .a(decimal_decoder_4_output[13]),
    .b(decimal_decoder_4_output[12]), .e(decimal_decoder_4_output[15]), .d(decimal_decoder_4_output_2[30]),
    .c(decimal_decoder_4_output_2[29]), .dp(decimal_decoder_4_output_2[28]));
  assign mar_1_out = OE ? in_5 : 4'bz;  // Controlled_Buffer controlled_buffer_4
  LED led_9 (.in(n8bit_alu_1_out_8[6]));
  LED led_10 (.in(n8bit_alu_1_out_8[7]));
  LED led_11 (.in(n8bit_alu_1_out_8[5]));
  _7_Segment_Display u_7_segment_display_11 (
    .g(decimal_decoder_4_output[11]), .f(decimal_decoder_4_output[10]), .a(decimal_decoder_4_output[9]),
    .b(decimal_decoder_4_output[8]), .e(decimal_decoder_4_output_2[27]), .d(decimal_decoder_4_output_2[26]),
    .c(decimal_decoder_4_output_2[25]), .dp(decimal_decoder_4_output_2[24]));
  _7_Segment_Display u_7_segment_display_12 (
    .g(decimal_decoder_4_output[7]), .f(decimal_decoder_4_output[6]), .a(decimal_decoder_4_output[5]),
    .b(decimal_decoder_4_output[4]), .e(decimal_decoder_4_output_2[23]), .d(decimal_decoder_4_output_2[22]),
    .c(decimal_decoder_4_output_2[21]), .dp(decimal_decoder_4_output_2[20]));
  LED led_12 (.in(n8bit_alu_1_out_8[3]));
  LED led_13 (.in(n8bit_alu_1_out_8[4]));
  LED led_14 (.in(n8bit_alu_1_out_8[2]));
  LED led_15 (.in(n8bit_alu_1_out_8[1]));
  _7_Segment_Display u_7_segment_display_13 (
    .g(decimal_decoder_4_output[3]), .f(decimal_decoder_4_output[2]), .a(decimal_decoder_4_output[1]),
    .b(decimal_decoder_4_output[0]), .e(decimal_decoder_4_output_2[19]), .d(decimal_decoder_4_output_2[18]),
    .c(decimal_decoder_4_output_2[17]), .dp(decimal_decoder_4_output_2[16]));
  LED led_16 (.in(n8bit_alu_1_out_8[0]));
  RAM #(.addrWidth(4), .bus("separate")) ram_1 (
    .addr(mar_1_out), .din(n8bit_alu_1_out_8), .data(n8bit_alu_1_out_8), .str(control_unit_1_1_c2),
    .clk(clock_1_out), .ld(control_unit_1_1_c3), .clr(in_7));  // open: sel
  BitSelector #(.group(4)) bitselector_2 (.in(out_17), .out(bitselector_2_out), .sel(1'b1));
  Counter #(.width(3), .max('h5)) counter_2 (.Q(out_25), .clk(clock_1_out));  // open: load, D, count, carry, clr
  assign bit_extender_2_out = {{5{1'b0}}, out_25};  // Bit_Extender bit_extender_2
  decimal_decoder decimal_decoder_5 (.Input(bit_extender_2_out), .Output(decimal_decoder_5_output));
  Control_Unit_1 control_unit_1_1 (
    .OP3(bitselector_2_out[3]), .OP2(bitselector_2_out[2]), .OP1(bitselector_2_out[1]),
    .OP0(bitselector_2_out[0]), .SC2(out_25[2]), .SC1(out_25[1]), .SC0(out_25[0]), .C0(control_unit_1_1_c0),
    .C1(control_unit_1_1_c1), .C2(control_unit_1_1_c2), .C3(control_unit_1_1_c3), .C4(control_unit_1_1_c4),
    .C5(control_unit_1_1_c5), .C6(control_unit_1_1_c6), .C7(control_unit_1_1_c7), .C8(control_unit_1_1_c8),
    .C9(control_unit_1_1_c9), .C10(control_unit_1_1_c10), .C11(control_unit_1_1_c11));
  Control_Unit_2 control_unit_2_1 (
    .OP3(bitselector_2_out[3]), .OP2(bitselector_2_out[2]), .OP1(bitselector_2_out[1]),
    .OP0(bitselector_2_out[0]), .SC2(out_25[2]), .SC1(out_25[1]), .SC0(out_25[0]),
    .C12(control_unit_2_1_c12), .C13(control_unit_2_1_c13), .C14(control_unit_2_1_c14),
    .C15(control_unit_2_1_c15));
  _7_Segment_Display u_7_segment_display_14 (
    .g(decimal_decoder_5_output[3]), .f(decimal_decoder_5_output[2]), .a(decimal_decoder_5_output[1]),
    .b(decimal_decoder_5_output[0]), .e(decimal_decoder_5_output[19]), .d(decimal_decoder_5_output[18]),
    .c(decimal_decoder_5_output[17]), .dp(decimal_decoder_5_output[16]));

  // Notes on the sheet:
  //   OE
  //   CE
  //   PC
  //   R1
  //   ALU
  //   R2
  //   IR
  //   Internal Data Bus
  //   MAR
  //      MBR
  //   Output R
  //   RAM
  //   Counter
endmodule

module register (
  input  [7:0] In,
  input  WE,
  input  CLK,
  input  Res,
  input  OE,
  output [7:0] Out,
  output [7:0] StoredD
);

  Register register_1 (.D(In), .en(WE), .Q(StoredD), .clk(CLK), .clr(Res));
  assign Out = OE ? StoredD : 8'bz;  // Controlled_Buffer controlled_buffer_1
endmodule

module mar (
  input  [3:0] In,
  input  WE,
  input  CLK,
  input  Res,
  input  OE,
  output [3:0] Out,
  output [3:0] Stored_D
);

  Register #(.width(4)) register_1 (.D(In), .en(WE), .Q(Stored_D), .clk(CLK), .clr(Res));
  assign Out = OE ? Stored_D : 4'bz;  // Controlled_Buffer controlled_buffer_1
endmodule

module _8bit_alu (
  input  in_1,
  input  in_2,
  input  [2:0] in_3,
  input  [7:0] in_4,
  input  [7:0] in_5,
  input  in_6,
  output [7:0] out_7,
  output [7:0] out_8,
  output out_9
);

  wire alu_1_c1, alu_2_c1, alu_3_c1, alu_4_c1, alu_5_c1, alu_6_c1, alu_7_c1;

  ALU alu_1 (.A(in_4[0]), .B(in_5[0]), .Cin(in_1), .Sub(in_2), .Output(out_7[0]), .c1(alu_1_c1), .in_4(in_3));
  ALU alu_2 (.A(in_4[1]), .B(in_5[1]), .Cin(alu_1_c1), .Sub(in_2), .Output(out_7[1]), .c1(alu_2_c1), .in_4(in_3));
  ALU alu_3 (.A(in_4[2]), .B(in_5[2]), .Cin(alu_2_c1), .Sub(in_2), .Output(out_7[2]), .c1(alu_3_c1), .in_4(in_3));
  ALU alu_4 (.A(in_4[3]), .B(in_5[3]), .Cin(alu_3_c1), .Sub(in_2), .Output(out_7[3]), .c1(alu_4_c1), .in_4(in_3));
  ALU alu_5 (.A(in_4[4]), .B(in_5[4]), .Cin(alu_4_c1), .Sub(in_2), .Output(out_7[4]), .c1(alu_5_c1), .in_4(in_3));
  ALU alu_6 (.A(in_4[5]), .B(in_5[5]), .Cin(alu_5_c1), .Sub(in_2), .Output(out_7[5]), .c1(alu_6_c1), .in_4(in_3));
  ALU alu_7 (.A(in_4[6]), .B(in_5[6]), .Cin(alu_6_c1), .Sub(in_2), .Output(out_7[6]), .c1(alu_7_c1), .in_4(in_3));
  ALU alu_8 (.A(in_4[7]), .B(in_5[7]), .Cin(alu_7_c1), .Sub(in_2), .Output(out_7[7]), .c1(out_9), .in_4(in_3));
  assign out_8 = in_6 ? out_7 : 8'bz;  // Controlled_Buffer controlled_buffer_1
endmodule

module ALU (
  input  A,
  input  B,
  input  Cin,
  input  [2:0] in_4,
  input  Sub,
  output Output,
  output c1
);

  wire adder_1_out, and_1_out, nand_1_out, nor_1_out, or_1_out, xor_1_out, xor_2_out;

  xor xor_1 (xor_1_out, Sub, B);
  and and_1 (and_1_out, A, B);
  or or_1 (or_1_out, A, B);
  xor xor_2 (xor_2_out, A, B);
  nand nand_1 (nand_1_out, A, B);
  nor nor_1 (nor_1_out, A, B);
  Adder #(.width(1)) adder_1 (.a(A), .b(xor_1_out), .out(adder_1_out), .cin(Cin), .cout(c1));
  Multiplexer #(.select(3), .enable("false")) multiplexer_1 (
    .in2(adder_1_out), .in3(nor_1_out), .in4(and_1_out), .in5(or_1_out), .in6(xor_2_out), .in7(nand_1_out),
    .out(Output), .sel(in_4));  // open: in0, in1
endmodule

module decimal_decoder (
  input  [7:0] Input,
  output [31:0] Output
);

  ROM #(.dataWidth(32)) rom_1 (
    .addr(Input),
    .data({Output[31:28], Output[15:12], Output[27:24], Output[11:8], Output[23:20], Output[7:4], Output[19:16], Output[3:0]}));  // open: sel

  // Notes on the sheet:
  //   contents of rom_1 (hex, n*v repeats v):
  //   e7 21 cb 6b 2d 6e ee 23 ef 2f 21e7 2121 21cb 216b 212d 216e 21ee 2123 21ef 212f cbe7 cb21 cbcb cb6b
  //   cb2d cb6e cbee cb23 cbef cb2f 6be7 6b21 6bcb 6b6b 6b2d 6b6e 6bee 6b23 6bef 6b2f 2de7 2d21 2dcb 2d6b
  //   2d2d 2d6e 2dee 2d23 2def 2d2f 6ee7 6e21 6ecb 6e6b 6e2d 6e6e 6eee 6e23 6eef 6e2f eee7 ee21 eecb ee6b
  //   ee2d ee6e eeee ee23 eeef ee2f 23e7 2321 23cb 236b 232d 236e 23ee 2323 23ef 232f efe7 ef21 efcb ef6b
  //   ef2d ef6e efee ef23 efef ef2f 2fe7 2f21 2fcb 2f6b 2f2d 2f6e 2fee 2f23 2fef 2f2f 21e7e7 21e721 21e7cb
  //   21e76b 21e72d 21e76e 21e7ee 21e723 21e7ef 21e72f 2121e7 212121 2121cb 21216b 21212d 21216e 2121ee
  //   212123 2121ef 21212f 21cbe7 21cb21 21cbcb 21cb6b 21cb2d 21cb6e 21cbee 21cb23 21cbef 21cb2f 216be7
  //   216b21 216bcb 216b6b 216b2d 216b6e 216bee 216b23 216bef 216b2f 212de7 212d21 212dcb 212d6b 212d2d
  //   212d6e 212dee 212d23 212def 212d2f 216ee7 216e21 216ecb 216e6b 216e2d 216e6e 216eee 216e23 216eef
  //   216e2f 21eee7 21ee21 21eecb 21ee6b 21ee2d 21ee6e 21eeee 21ee23 21eeef 21ee2f 2123e7 212321 2123cb
  //   21236b 21232d 21236e 2123ee 212323 2123ef 21232f 21efe7 21ef21 21efcb 21ef6b 21ef2d 21ef6e 21efee
  //   21ef23 21efef 21ef2f 212fe7 212f21 212fcb 212f6b 212f2d 212f6e 212fee 212f23 212fef 212f2f cbe7e7
  //   cbe721 cbe7cb cbe76b cbe72d cbe76e cbe7ee cbe723 cbe7ef cbe72f cb21e7 cb2121 cb21cb cb216b cb212d
  //   cb216e cb21ee cb2123 cb21ef cb212f cbcbe7 cbcb21 cbcbcb cbcb6b cbcb2d cbcb6e cbcbee cbcb23 cbcbef
  //   cbcb2f cb6be7 cb6b21 cb6bcb cb6b6b cb6b2d cb6b6e cb6bee cb6b23 cb6bef cb6b2f cb2de7 cb2d21 cb2dcb
  //   cb2d6b cb2d2d cb2d6e cb2dee cb2d23 cb2def cb2d2f cb6ee7 cb6e21 cb6ecb cb6e6b cb6e2d cb6e6e
endmodule

module Control_Unit_1 (
  input  OP3,
  input  OP2,
  input  OP1,
  input  OP0,
  input  SC2,
  input  SC1,
  input  SC0,
  output C0,
  output C1,
  output C2,
  output C3,
  output C4,
  output C5,
  output C6,
  output C7,
  output C8,
  output C9,
  output C10,
  output C11
);

  wire and_5_out, and_6_out, and_7_out, and_8_out, and_9_out, and_10_out, and_11_out, and_13_out, and_14_out,
       and_15_out, and_16_out, and_17_out, and_18_out, and_19_out, not_1_out, not_2_out, not_3_out,
       not_4_out, not_5_out, not_6_out, not_7_out, not_8_out, not_9_out, not_10_out, not_11_out, not_12_out,
       not_13_out, not_14_out, not_15_out, not_16_out, not_17_out, not_18_out, not_19_out, not_20_out,
       not_21_out, not_22_out, not_23_out, not_24_out;

  not not_1 (not_1_out, SC2);
  not not_2 (not_2_out, SC1);
  not not_3 (not_3_out, SC0);
  not not_4 (not_4_out, SC2);
  not not_5 (not_5_out, SC1);
  and and_1 (C2, OP1, SC2);
  not not_6 (not_6_out, SC2);
  not not_7 (not_7_out, SC1);
  not not_8 (not_8_out, OP1);
  not not_9 (not_9_out, SC0);
  not not_10 (not_10_out, SC2);
  not not_11 (not_11_out, SC1);
  not not_12 (not_12_out, OP1);
  not not_13 (not_13_out, SC0);
  not not_14 (not_14_out, SC0);
  and and_2 (C6, OP1, SC2);
  not not_15 (not_15_out, SC0);
  not not_16 (not_16_out, OP1);
  not not_17 (not_17_out, SC2);
  not not_18 (not_18_out, SC1);
  not not_19 (not_19_out, SC0);
  not not_20 (not_20_out, OP1);
  not not_21 (not_21_out, SC2);
  not not_22 (not_22_out, SC1);
  not not_23 (not_23_out, SC0);
  not not_24 (not_24_out, OP0);
  and and_3 (C0, not_1_out, not_2_out, not_3_out);
  and and_4 (C1, not_4_out, not_5_out, SC0);
  and and_5 (and_5_out, not_6_out, not_7_out, SC0);
  and and_6 (and_6_out, not_8_out, SC2, not_9_out);
  and and_7 (and_7_out, not_10_out, not_11_out, SC0);
  and and_8 (and_8_out, not_12_out, SC2, not_13_out);
  and and_9 (and_9_out, OP1, OP0, SC0);
  and and_10 (and_10_out, SC1, not_14_out);
  and and_11 (and_11_out, SC2, SC0);
  and and_12 (C7, SC1, not_15_out);
  and and_13 (and_13_out, not_16_out, SC1, SC0);
  and and_14 (and_14_out, OP0, SC1, SC0);
  and and_15 (and_15_out, not_17_out, not_18_out, not_19_out);
  and and_16 (and_16_out, not_20_out, SC1, SC0);
  and and_17 (and_17_out, OP0, SC1, SC0);
  and and_18 (and_18_out, not_21_out, not_22_out, SC0);
  and and_19 (and_19_out, SC2, not_23_out);
  and and_20 (C11, OP1, not_24_out, SC1, SC0);
  or or_1 (C3, and_5_out, and_6_out);
  or or_2 (C4, and_7_out, and_8_out, and_9_out);
  or or_3 (C5, and_10_out, and_11_out);
  or or_4 (C8, and_13_out, and_14_out);
  or or_5 (C9, and_15_out, and_16_out, and_17_out);
  or or_6 (C10, and_18_out, and_19_out);
endmodule

module Control_Unit_2 (
  input  OP3,
  input  OP2,
  input  OP1,
  input  OP0,
  input  SC2,
  input  SC1,
  input  SC0,
  output C12,
  output C13,
  output C14,
  output C15
);

  wire not_1_out, not_2_out;

  not not_1 (not_1_out, OP0);
  and and_1 (C13, OP0, SC2, SC0);
  and and_2 (C14, OP1, OP0, SC1, SC0);
  not not_2 (not_2_out, OP0);
  and and_3 (C12, not_1_out, SC2, SC0);
  and and_4 (C15, OP1, not_2_out, SC1, SC0);
endmodule

module main2 (
  input  OE,
  input  CE,
  input  [7:0] data_test,
  input  OE_2,
  input  Res,
  input  in_6,
  input  [3:0] in_7,
  input  in_8,
  input  in_9,
  input  in_10,
  input  in_11,
  input  WE,
  input  in_13,
  input  in_14,
  input  in_15,
  input  in_16,
  input  OE_3,
  input  MBR,
  input  in_19,
  input  in_20,
  input  in_21,
  input  in_22,
  input  [2:0] in_23,
  input  in_24,
  input  in_25,
  input  in_26,
  input  in_27,
  input  in_28,
  input  in_29,
  output [3:0] out_30,
  output [3:0] out_31,
  output [7:0] out_32,
  output [7:0] out_33,
  output [7:0] out_34,
  output [7:0] out_35,
  output [7:0] out_36,
  output [7:0] Com,
  output out_38,
  output [7:0] out_39
);

  wire and_1_out, clock_1_out, comparator_1_eq, not_1_out;
  wire [3:0] controlled_buffer_1_out, Halt, mar_1_out;
  wire [7:0] bit_extender_1_out, n8bit_alu_1_out_8, register_3_out;
  wire [15:0] decimal_decoder_4_output;
  wire [30:16] decimal_decoder_4_output_2;
  wire [31:0] decimal_decoder_1_output, decimal_decoder_2_output, decimal_decoder_3_output;

  Clock clock_1 (.out(clock_1_out));
  Comparator #(.width(4)) comparator_1 (.a(4'b1111), .b(Halt), .eq(comparator_1_eq));  // open: gt, lt
  not not_1 (not_1_out, comparator_1_eq);
  and and_1 (and_1_out, clock_1_out, not_1_out);
  assign controlled_buffer_1_out = OE ? out_30 : 4'bz;  // Controlled_Buffer controlled_buffer_1
  Counter #(.width(4), .max('h3)) counter_1 (
    .D(controlled_buffer_1_out), .count(CE), .Q(out_30), .clk(and_1_out), .clr(Res));  // open: load, carry
  register register_1 (
    .In(n8bit_alu_1_out_8), .WE(in_19), .CLK(and_1_out), .Res(in_20), .StoredD(out_34));  // open: OE, Out
  register register_2 (
    .In(n8bit_alu_1_out_8), .WE(in_28), .CLK(and_1_out), .Res(in_29), .StoredD(out_39));  // open: OE, Out
  assign bit_extender_1_out = {{4{1'b0}}, out_30};  // Bit_Extender bit_extender_1
  decimal_decoder decimal_decoder_1 (.Input(out_34), .Output(decimal_decoder_1_output));
  _8bit_alu u_8bit_alu_1 (
    .in_4(out_34), .in_5(out_39), .in_2(in_21), .in_1(in_22), .in_3(in_23), .out_7(out_35),
    .out_8(n8bit_alu_1_out_8), .in_6(in_26), .out_9(out_38));
  decimal_decoder decimal_decoder_2 (.Input(bit_extender_1_out), .Output(decimal_decoder_2_output));
  register register_3 (
    .In(n8bit_alu_1_out_8), .WE(in_11), .CLK(and_1_out), .Res(in_13), .OE(in_14), .Out(register_3_out),
    .StoredD(out_32));
  decimal_decoder decimal_decoder_3 (.Input(out_39), .Output(decimal_decoder_3_output));
  _7_Segment_Display u_7_segment_display_1 (
    .g(decimal_decoder_2_output[3]), .f(decimal_decoder_2_output[2]), .a(decimal_decoder_2_output[1]),
    .b(decimal_decoder_2_output[0]), .e(decimal_decoder_2_output[19]), .d(decimal_decoder_2_output[18]),
    .c(decimal_decoder_2_output[17]), .dp(decimal_decoder_2_output[16]));
  BitSelector #(.group(4)) bitselector_1 (.in(out_32), .out(Halt), .sel(1'b1));
  _7_Segment_Display u_7_segment_display_2 (
    .g(decimal_decoder_1_output[15]), .f(decimal_decoder_1_output[14]), .a(decimal_decoder_1_output[13]),
    .b(decimal_decoder_1_output[12]), .e(decimal_decoder_1_output[31]), .d(decimal_decoder_1_output[30]),
    .c(decimal_decoder_1_output[29]), .dp(decimal_decoder_1_output[28]));
  _7_Segment_Display u_7_segment_display_3 (
    .g(decimal_decoder_1_output[11]), .f(decimal_decoder_1_output[10]), .a(decimal_decoder_1_output[9]),
    .b(decimal_decoder_1_output[8]), .e(decimal_decoder_1_output[27]), .d(decimal_decoder_1_output[26]),
    .c(decimal_decoder_1_output[25]), .dp(decimal_decoder_1_output[24]));
  _7_Segment_Display u_7_segment_display_4 (
    .g(decimal_decoder_1_output[3]), .f(decimal_decoder_1_output[2]), .a(decimal_decoder_1_output[1]),
    .b(decimal_decoder_1_output[0]), .e(decimal_decoder_1_output[19]), .d(decimal_decoder_1_output[18]),
    .c(decimal_decoder_1_output[17]), .dp(decimal_decoder_1_output[16]));
  _7_Segment_Display u_7_segment_display_5 (
    .g(decimal_decoder_1_output[7]), .f(decimal_decoder_1_output[6]), .a(decimal_decoder_1_output[5]),
    .b(decimal_decoder_1_output[4]), .e(decimal_decoder_1_output[23]), .d(decimal_decoder_1_output[22]),
    .c(decimal_decoder_1_output[21]), .dp(decimal_decoder_1_output[20]));
  _7_Segment_Display u_7_segment_display_6 (
    .g(decimal_decoder_3_output[11]), .f(decimal_decoder_3_output[10]), .a(decimal_decoder_3_output[8]),
    .b(decimal_decoder_3_output[8]), .e(decimal_decoder_3_output[27]), .d(decimal_decoder_3_output[26]),
    .c(decimal_decoder_3_output[25]), .dp(decimal_decoder_3_output[24]));
  _7_Segment_Display u_7_segment_display_7 (
    .g(decimal_decoder_3_output[15]), .f(decimal_decoder_3_output[14]), .a(decimal_decoder_3_output[13]),
    .b(decimal_decoder_3_output[12]), .e(decimal_decoder_3_output[31]), .d(decimal_decoder_3_output[30]),
    .c(decimal_decoder_3_output[29]), .dp(decimal_decoder_3_output[28]));
  _7_Segment_Display u_7_segment_display_8 (
    .g(decimal_decoder_3_output[7]), .f(decimal_decoder_3_output[6]), .a(decimal_decoder_3_output[5]),
    .b(decimal_decoder_3_output[4]), .e(decimal_decoder_3_output[23]), .d(decimal_decoder_3_output[22]),
    .c(decimal_decoder_3_output[21]), .dp(decimal_decoder_3_output[20]));
  _7_Segment_Display u_7_segment_display_9 (
    .g(decimal_decoder_3_output[3]), .f(decimal_decoder_3_output[2]), .a(decimal_decoder_3_output[1]),
    .b(decimal_decoder_3_output[0]), .e(decimal_decoder_3_output[19]), .d(decimal_decoder_3_output[18]),
    .c(decimal_decoder_3_output[17]), .dp(decimal_decoder_3_output[16]));
  BitSelector #(.group(4)) bitselector_2 (.in(register_3_out), .out(controlled_buffer_1_out), .sel(1'b0));
  LED led_1 (.in(n8bit_alu_1_out_8[7]));
  LED led_2 (.in(n8bit_alu_1_out_8[5]));
  LED led_3 (.in(n8bit_alu_1_out_8[6]));
  assign n8bit_alu_1_out_8 = in_6 ? data_test : 8'bz;  // Controlled_Buffer controlled_buffer_2
  LED led_4 (.in(n8bit_alu_1_out_8[3]));
  LED led_5 (.in(n8bit_alu_1_out_8[2]));
  LED led_6 (.in(n8bit_alu_1_out_8[4]));
  LED led_7 (.in(n8bit_alu_1_out_8[0]));
  LED led_8 (.in(n8bit_alu_1_out_8[1]));
  assign n8bit_alu_1_out_8 = in_9 ? out_33 : 8'bz;  // Controlled_Buffer controlled_buffer_3
  mar mar_1 (
    .In(controlled_buffer_1_out), .WE(in_8), .CLK(and_1_out), .OE(in_10), .Out(mar_1_out), .Stored_D(out_31));  // open: Res
  register register_4 (
    .In(n8bit_alu_1_out_8), .WE(in_15), .CLK(and_1_out), .Res(in_16), .OE(MBR), .Out(n8bit_alu_1_out_8),
    .StoredD(out_33));
  register register_5 (
    .In(n8bit_alu_1_out_8), .WE(in_24), .CLK(and_1_out), .OE(in_25), .Out(n8bit_alu_1_out_8), .StoredD(out_36));  // open: Res
  decimal_decoder decimal_decoder_4 (
    .Input(out_36),
    .Output({decimal_decoder_4_output[15], decimal_decoder_4_output_2, decimal_decoder_4_output}));
  assign Com = in_27 ? ~out_36 : 8'bz;  // Controlled_Inverter controlled_inverter_1
  _7_Segment_Display u_7_segment_display_10 (
    .g(decimal_decoder_4_output[15]), .f(decimal_decoder_4_output[14]), .a(decimal_decoder_4_output[13]),
    .b(decimal_decoder_4_output[12]), .e(decimal_decoder_4_output[15]), .d(decimal_decoder_4_output_2[30]),
    .c(decimal_decoder_4_output_2[29]), .dp(decimal_decoder_4_output_2[28]));
  assign mar_1_out = OE_2 ? in_7 : 4'bz;  // Controlled_Buffer controlled_buffer_4
  LED led_9 (.in(n8bit_alu_1_out_8[7]));
  LED led_10 (.in(n8bit_alu_1_out_8[5]));
  LED led_11 (.in(n8bit_alu_1_out_8[6]));
  _7_Segment_Display u_7_segment_display_11 (
    .g(decimal_decoder_4_output[7]), .f(decimal_decoder_4_output[6]), .a(decimal_decoder_4_output[5]),
    .b(decimal_decoder_4_output[4]), .e(decimal_decoder_4_output_2[23]), .d(decimal_decoder_4_output_2[22]),
    .c(decimal_decoder_4_output_2[21]), .dp(decimal_decoder_4_output_2[20]));
  _7_Segment_Display u_7_segment_display_12 (
    .g(decimal_decoder_4_output[11]), .f(decimal_decoder_4_output[10]), .a(decimal_decoder_4_output[9]),
    .b(decimal_decoder_4_output[8]), .e(decimal_decoder_4_output_2[27]), .d(decimal_decoder_4_output_2[26]),
    .c(decimal_decoder_4_output_2[25]), .dp(decimal_decoder_4_output_2[24]));
  LED led_12 (.in(n8bit_alu_1_out_8[2]));
  LED led_13 (.in(n8bit_alu_1_out_8[3]));
  LED led_14 (.in(n8bit_alu_1_out_8[4]));
  LED led_15 (.in(n8bit_alu_1_out_8[1]));
  _7_Segment_Display u_7_segment_display_13 (
    .g(decimal_decoder_4_output[3]), .f(decimal_decoder_4_output[2]), .a(decimal_decoder_4_output[1]),
    .b(decimal_decoder_4_output[0]), .e(decimal_decoder_4_output_2[19]), .d(decimal_decoder_4_output_2[18]),
    .c(decimal_decoder_4_output_2[17]), .dp(decimal_decoder_4_output_2[16]));
  LED led_16 (.in(n8bit_alu_1_out_8[0]));
  RAM #(.addrWidth(4), .bus("separate")) ram_1 (
    .addr(mar_1_out), .din(n8bit_alu_1_out_8), .data(n8bit_alu_1_out_8), .str(WE), .clk(and_1_out), .ld(OE_3));  // open: sel, clr

  // Notes on the sheet:
  //   PC
  //   R1
  //   ALU
  //   R2
  //   IR
  //   Internal Data Bus
  //   MAR
  //   Output R
  //   RAM
endmodule

module modified_alu (
  input  A,
  input  B,
  input  Cin,
  input  [2:0] in_4,
  input  Sub,
  output Output,
  output c1
);

  wire adder_1_out, and_1_out, nand_1_out, or_1_out, xor_1_out, xor_2_out;

  xor xor_1 (xor_1_out, Sub, B);
  and and_1 (and_1_out, A, B);
  or or_1 (or_1_out, A, B);
  xor xor_2 (xor_2_out, A, B);
  nand nand_1 (nand_1_out, A, B);
  // NOR_Gate nor_1 has open pins: in0=A, in1=B, out=open
  Adder #(.width(1)) adder_1 (.a(A), .b(xor_1_out), .out(adder_1_out), .cin(Cin), .cout(c1));
  Multiplexer #(.select(3), .enable("false")) multiplexer_1 (
    .in2(adder_1_out), .in4(and_1_out), .in5(or_1_out), .in6(xor_2_out), .in7(nand_1_out), .out(Output),
    .sel(in_4));  // open: in0, in1, in3
endmodule
